# Fritzing sketch wm-temperature-esp8266 (saved by Fritzing 0.9.3b)
breadboards: 2

parts:
  U1 = NodeMCU V1.0
  T1 = LM35 Temperature Sensor [package="TO92 [THT]"]

nets:
  N1: U1.3V3, T1.+Vs
  GND: U1.GND, T1.GND
  N2: U1.A0, T1.Vout

custom parts:
  NodeMCU V1.0: ESP8266 based NodeMCU
